# Fritzing sketch Fritzing (saved by Fritzing 0.9.0b)
breadboards: 1

parts:
  Composant1 = Spark Core (v1.0)
  PING)))_SENSOR1 = PING))) SENSOR
  R1 = Resistor [package="2512 [SMD]"]
  LED1 = LED - 5mm [color="Red (633nm)" package="5 mm [THT]"]
  J1 = Piezo Speaker

nets:
  GND: Composant1.GND, PING)))_SENSOR1.GND, LED1.cathode, J1.pin1
  N1: Composant1.D0, R1.Pin_1
  N2: Composant1.D1, J1.pin2
  N3: Composant1.D7, Composant1.3V3*, PING)))_SENSOR1.5V, PING)))_SENSOR1.SIGNAL
  N4: R1.Pin_0, LED1.anode
